# Fritzing sketch Uno_DRV8833_HC-06 (saved by Fritzing 0.9.3b)

parts:
  DRV8833 = Adafruit DRV8833 DC/Stepper Motor Driver [part_number="Adafruit #3297"]
  R1 = Resistor [tolerance=±5% resistance=1k package=THT]
  R2 = Resistor [tolerance=±5% resistance=3.3k package=THT]
  M1 = DC Motor
  M2 = DC Motor
  DC = Power plug
  Uno = Arduino Uno (Rev3)
  HC-06 = Bluetooth HC-05 Macho

nets:
  N1: DRV8833.PWRIN, DC.VCC
  GND: DRV8833.GND, R2.Pin_0, DC.GND, Uno.GND, HC-06.GND
  N2: DRV8833.AOUT2, M2.pin_2
  N3: DRV8833.AOUT1, M2.pin_1
  N4: DRV8833.BOUT1, M1.pin_2
  N5: DRV8833.BOUT2, M1.pin_1
  N6: DRV8833.BIN1, Uno.D3_PWM
  N7: DRV8833.BIN2, Uno.D5_PWM
  N8: DRV8833.AIN2, Uno.D9_PWM
  N9: DRV8833.AIN1, Uno.D6_PWM
  N10: R1.Pin_0, R2.Pin_1, HC-06.RXD
  N11: R1.Pin_1, Uno.D1/TX
  N12: Uno.D0/RX, HC-06.TXD
  5V: Uno.5V, HC-06.VCC

custom parts:
  Adafruit DRV8833 DC/Stepper Motor Driver: Spin two DC motors or step one bi-polar or uni-polar stepper with up to 1.2A per channel using the DRV8833. This motor driver chip is a nice alternative to the TB6612 driver. Like that chip, you get 2 full H-bridges, but this chip is better for low voltage uses (can run from 2.7V up to 10.8V motor power) and has built in current limiting capability. We set it up for 1A current limiting so you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
